# Fritzing sketch IoTSkematik2 (saved by Fritzing 0.9.9b)
breadboards: 1

parts:
  Part1 = IFR520 MOS module [package=THT]
  Part2 = IFR520 MOS module [package=THT]
  M1 = Stepper Motor - Bipolar  # not connected
  R1 = Temperature Sensor (Thermistor) [thermistor_type=NTC package=THT]
  Part3 = Photon
  DC1 = DC_DC_XL4016 [package=board_screw]
  U1 = LIPO-2000mAh [package=lipo-2000]
  R2 = Resistor [tolerance=±5% resistance=596 power=0.25 package=THT]

nets:
  N1: Part1.SIG, Part3.D7
  GND: Part1.GND, Part2.GND, R1.pin_1, Part3.GND, DC1.OUT-
  VIN: Part1.VIN, Part2.VIN, DC1.OUT+
  N2: Part2.SIG, Part3.D6
  N3: R1.pin_0, Part3.A0, R2.Pin_1
  N4: DC1.IN+, U1.+
  N5: DC1.IN-, U1.-

notes:
  3.6 V MODEL TLP-93111/A/
  eller Powerbanken PB20A 5V
  XL6009 DC-DC Convertor modul
  Particle Photon2
  PT500 temperaturføleren
  M3P 46825-30 aktuatoren
  Powerbanken PB20A Kapacitet: 10.000 mAh, 3,7 V, 37 Wh eller Longlife batteri TLP-93111/A
  XL6009 DC-DC
  IRF520 Power MOSFET
  M3P 46825-30 aktuatoren
